# Fritzing sketch sketch (saved by Fritzing 0.9.3b)

parts:
  Raspberry_Pi_1 = Raspberry Pi 3 [part_number=RPI-3-V1.2]
  neopixel1 = Neopixel Ring 16
  neopixel2 = Neopixel 24 Ring
  S1 = Round Pushbutton

nets:
  N1: Raspberry_Pi_1.GIPO13, neopixel2.IN
  N2: Raspberry_Pi_1.GIPO23, S1.leg1
  GND: Raspberry_Pi_1.GND, neopixel1.GND, neopixel2.GND, S1.leg0
  VCC: Raspberry_Pi_1.5V, neopixel1.VCC, neopixel2.Vcc
  N3: neopixel1.IN, neopixel2.OUT

custom parts:
  Neopixel Ring 16: Neopixel Ring x16
